// Logisim project cpu.circ as structural Verilog: 8 circuits, main circuit main
module main (
  input  Clear_RAM,
  input  Clear_TTY
);

  wire and_1_out, clock_1_out, controlled_buffer_1_out, CPU_write, Input_read_from_keyboard,
       keyboard_1_avail, Log_clock_for_tty, not_1_out;
  wire [6:0] keyboard_1_data, Log_output;
  wire [7:0] A;
  wire [23:0] CPU_data_out, D, Input_to_cpu;
  wire [23:7] Log_output_2;

  Clock clock_1 (.out(clock_1_out));
  and and_1 (and_1_out, clock_1_out, Input_read_from_keyboard);
  Keyboard keyboard_1 (
    .clk(controlled_buffer_1_out), .re(keyboard_1_avail), .avail(keyboard_1_avail), .data(keyboard_1_data));  // open: clr
  assign controlled_buffer_1_out = keyboard_1_avail ? and_1_out : 1'bz;  // Controlled_Buffer controlled_buffer_1
  CPU CPU (
    .Clock(clock_1_out), .Data_In(Input_to_cpu), .Data_Out(CPU_data_out), .Write(CPU_write), .RAM_Address(A));  // open: Read
  Input Input (
    .To_CPU(Input_to_cpu), .RAM_Address(A), .From_RAM(D), .Keyboard_Input({{17{1'b0}}, keyboard_1_data}),
    .Read_from_Keyboard(Input_read_from_keyboard));
  assign D = CPU_write ? CPU_data_out : 24'bz;  // Controlled_Buffer controlled_buffer_2
  TTY #(.trigger("falling")) tty_1 (.data(Log_output), .clk(Log_clock_for_tty), .clr(Clear_TTY));  // open: we
  not not_1 (not_1_out, CPU_write);
  RAM #(.dataWidth(24), .bus("asynch")) ram_1 (.addr(A), .data(D), .ld(not_1_out), .clr(Clear_RAM));  // open: sel
  Log Log (
    .Data(D), .Write(CPU_write), .RAM_Address(A), .Output({Log_output_2, Log_output}),
    .Clock_for_TTY(Log_clock_for_tty));
  DotMatrix #(.inputtype("row"), .matrixcols(24), .matrixrows(1)) dotmatrix_1 (.row0(D));
  DotMatrix #(.inputtype("row"), .matrixcols(8), .matrixrows(1)) dotmatrix_2 (.row0(A));

  // Notes on the sheet:
  //   Keyboard
  //   Blinkenlights
  //   Address Bus
  //   Data Bus
endmodule

module Stepper (
  input  Clock,
  output Step_0,
  output Step_1,
  output Step_2,
  output Step_3
);

  wire not_1_out, not_2_out, not_3_out, not_4_out;
  wire [1:0] adder_1_out, register_1_q;

  Register #(.width(2)) register_1 (.D(adder_1_out), .Q(register_1_q), .clk(Clock));  // open: en, clr
  Adder #(.width(2)) adder_1 (.a(2'b01), .b(register_1_q), .out(adder_1_out));  // open: cin, cout
  not not_1 (not_1_out, register_1_q[0]);
  not not_2 (not_2_out, register_1_q[1]);
  not not_3 (not_3_out, register_1_q[1]);
  not not_4 (not_4_out, register_1_q[0]);
  and and_1 (Step_0, not_1_out, not_2_out);
  and and_2 (Step_1, register_1_q[0], not_3_out);
  and and_3 (Step_2, not_4_out, register_1_q[1]);
  and and_4 (Step_3, register_1_q[0], register_1_q[1]);
endmodule

module PC_Area (
  input  [7:0] C_Address,
  input  Jump,
  input  Update,
  output [7:0] Instruction_Address
);

  wire [7:0] adder_1_out, multiplexer_1_out;

  Register register_1 (.D(multiplexer_1_out), .Q(Instruction_Address), .clk(Update));  // open: en, clr
  Multiplexer #(.width(8)) multiplexer_1 (
    .in0(adder_1_out), .in1(C_Address), .out(multiplexer_1_out), .sel(Jump));  // open: en
  Adder adder_1 (.a(Instruction_Address), .b(8'h1), .out(adder_1_out));  // open: cin, cout
endmodule

module ALU (
  input  [23:0] From_Reg__B,
  input  [23:0] From_Reg__A,
  output [23:0] Result,
  output Result__0
);

  wire comparator_1_eq, comparator_1_lt;

  Subtractor #(.width(24)) subtractor_1 (.a(From_Reg__B), .b(From_Reg__A), .out(Result));  // open: bin, bout
  Comparator #(.width(24)) comparator_1 (
    .a(Result), .b({24{1'b0}}), .eq(comparator_1_eq), .lt(comparator_1_lt));  // open: gt
  or or_1 (Result__0, comparator_1_eq, comparator_1_lt);
endmodule

module RAM_Inter (
  input  [7:0] A,
  input  [7:0] B,
  input  [7:0] C,
  input  [23:0] Result,
  input  Jump,
  input  Step_0,
  input  Step_1,
  input  Step_2,
  input  Step_3,
  output [23:0] Data_Out,
  output Read,
  output Write,
  output [7:0] RAM_Address
);

  wire or_1_out;
  wire [7:0] PC_Area_instruction_address;

  assign RAM_Address = Step_0 ? PC_Area_instruction_address : 8'bz;  // Controlled_Buffer controlled_buffer_1
  PC_Area PC_Area (.C_Address(C), .Jump(Jump), .Update(Step_3), .Instruction_Address(PC_Area_instruction_address));
  assign RAM_Address = Step_1 ? A : 8'bz;  // Controlled_Buffer controlled_buffer_2
  assign RAM_Address = or_1_out ? B : 8'bz;  // Controlled_Buffer controlled_buffer_3
  or or_1 (or_1_out, Step_2, Step_3);
  assign Data_Out = Step_3 ? Result : 24'bz;  // Controlled_Buffer controlled_buffer_4
  not not_1 (Read, Step_3);

  assign Write = Step_3;
endmodule

module CPU (
  input  [23:0] Data_In,
  input  Clock,
  output [23:0] Data_Out,
  output Read,
  output Write,
  output [7:0] RAM_Address
);

  wire ALU_result__0, Stepper_step_0, Stepper_step_1, Stepper_step_2, Stepper_step_3;
  wire [23:0] AR, B_A, BR, IR;

  Register #(.width(24), .trigger("high")) register_1 (.D(Data_In), .Q(AR), .clk(Stepper_step_1));  // open: en, clr
  Stepper Stepper (
    .Clock(Clock), .Step_0(Stepper_step_0), .Step_1(Stepper_step_1), .Step_2(Stepper_step_2),
    .Step_3(Stepper_step_3));
  DotMatrix #(.inputtype("row"), .matrixcols(24), .matrixrows(1)) dotmatrix_1 (.row0(IR));
  DotMatrix #(.inputtype("row"), .matrixcols(24), .matrixrows(1)) dotmatrix_2 (.row0(AR));
  DotMatrix #(.inputtype("row"), .matrixcols(24), .matrixrows(1)) dotmatrix_3 (.row0(BR));
  DotMatrix #(.inputtype("row"), .matrixcols(24), .matrixrows(1)) dotmatrix_4 (.row0(B_A));
  Register #(.width(24), .trigger("high")) register_2 (.D(Data_In), .Q(BR), .clk(Stepper_step_2));  // open: en, clr
  ALU ALU (.From_Reg__B(BR), .From_Reg__A(AR), .Result(B_A), .Result__0(ALU_result__0));
  Register #(.width(24), .trigger("high")) register_3 (.D(Data_In), .Q(IR), .clk(Stepper_step_0));  // open: en, clr
  RAM_Inter ram_inter_1 (
    .A(IR[23:16]), .B(IR[15:8]), .C(IR[7:0]), .Result(B_A), .Jump(ALU_result__0), .Step_0(Stepper_step_0),
    .Step_1(Stepper_step_1), .Step_2(Stepper_step_2), .Step_3(Stepper_step_3), .Data_Out(Data_Out),
    .Read(Read), .Write(Write), .RAM_Address(RAM_Address));

  // Notes on the sheet:
  //   Reg. A
  //   Reg. B
  //   Inst. Reg.
  //   Blinkenlights
  //   Instruction Register
  //   A Register
  //   B Register
  //   ALU Result
endmodule

module Log (
  input  [23:0] Data,
  input  Write,
  input  [7:0] RAM_Address,
  output [23:0] Output,
  output Clock_for_TTY
);

  wire comparator_1_eq, not_1_out, not_2_out;
  wire [7:0] adder_1_out, register_1_q, shifter_1_out;

  Register register_1 (.D(adder_1_out), .Q(register_1_q), .clk(not_1_out));  // open: en, clr
  Comparator comparator_1 (.a(RAM_Address), .b({8{1'b1}}), .eq(comparator_1_eq));  // open: gt, lt
  Adder adder_1 (.a(8'h1), .b(register_1_q), .out(adder_1_out));  // open: cin, cout
  and and_1 (Clock_for_TTY, Write, comparator_1_eq);
  not not_1 (not_1_out, Clock_for_TTY);
  assign Output = Clock_for_TTY ? Data : 24'bz;  // Controlled_Buffer controlled_buffer_1
  Shifter #(.shift("lr")) shifter_1 (.in(register_1_q), .\dist (3'b001), .out(shifter_1_out));
  not not_2 (not_2_out, Clock_for_TTY);
  RAM #(.dataWidth(24), .bus("asynch")) ram_1 (.addr(shifter_1_out), .data(Output), .ld(not_2_out));  // open: sel, clr

  // Notes on the sheet:
  //   This component stores outputs from CPU.
endmodule

module Input (
  input  [23:0] From_RAM,
  input  [7:0] RAM_Address,
  input  [23:0] Keyboard_Input,
  output [23:0] To_CPU,
  output Read_from_Keyboard
);

  Multiplexer #(.width(24)) multiplexer_1 (
    .in0(From_RAM), .in1(Keyboard_Input), .out(To_CPU), .sel(Read_from_Keyboard));  // open: en
  Comparator comparator_1 (.a(8'hfe), .b(RAM_Address), .eq(Read_from_Keyboard));  // open: gt, lt
endmodule
